# Fritzing sketch raspiledmeter (saved by Fritzing 0.7.7b)
breadboards: 1

parts:
  R1 = Resistor [tolerance=±5% resistance=330 package=THT]
  R2 = Resistor [tolerance=±5% resistance=330 package=THT]
  R3 = Resistor [tolerance=±5% resistance=330 package=THT]
  R4 = Resistor [tolerance=±5% resistance=330 package=THT]
  R6 = Resistor [tolerance=±5% resistance=330 package=THT]
  R7 = Resistor [tolerance=±5% resistance=330 package=THT]
  R8 = Resistor [tolerance=±5% resistance=330 package=THT]
  R9 = Resistor [tolerance=±5% resistance=330 package=THT]
  LED1 = LED - 5mm [color="Green (555nm)" package="5 mm [THT]"]
  LED3 = LED - 5mm [color="Green (555nm)" package="5 mm [THT]"]
  LED4 = LED - 5mm [color="Green (555nm)" package="5 mm [THT]"]
  LED5 = LED - 5mm [color="Yellow (585nm)" package="5 mm [THT]"]
  LED6 = LED - 5mm [color="Green (555nm)" package="5 mm [THT]"]
  LED7 = LED - 5mm [color="Yellow (585nm)" package="5 mm [THT]"]
  LED8 = smd LED [color="Red (633nm)" package="1206 [SMD]"]
  LED9 = LED - 5mm [color="Green (555nm)" package="5 mm [THT]"]
  RaspberryPi1 = Raspberry Pi Model B

nets:
  N1: R1.Pin_0, RaspberryPi1.#17
  N2: R1.Pin_1, LED6.anode
  N3: R2.Pin_0, RaspberryPi1.#23
  N4: R2.Pin_1, LED7.anode
  N5: R3.Pin_0, RaspberryPi1.#21
  N6: R3.Pin_1, LED4.anode
  N7: R4.Pin_0, RaspberryPi1.#25
  N8: R4.Pin_1, LED8.anode
  N9: R6.Pin_0, RaspberryPi1.#4
  N10: R6.Pin_1, LED3.anode
  N11: R7.Pin_0, RaspberryPi1.#24
  N12: R7.Pin_1, LED5.anode
  N13: R8.Pin_0, RaspberryPi1.#18
  N14: R8.Pin_1, LED1.anode
  N15: R9.Pin_0, RaspberryPi1.#22
  N16: R9.Pin_1, LED9.anode
  N17: LED1.cathode, LED3.cathode, LED4.cathode, LED5.cathode, LED6.cathode, LED7.cathode, LED8.cathode, LED9.cathode, RaspberryPi1.GND

custom parts:
  Raspberry Pi Model B: Raspberry Pi (Model B)
